# Fritzing sketch esquemaProjeto4 (saved by Fritzing 0.7.10b)
breadboards: 1

parts:
  Arduino1 = Arduino
  R1 = Resistor [tolerance=±5% resistance=220 package=THT]
  R2 = Resistor [tolerance=±5% resistance=220 package=THT]
  R3 = Resistor [tolerance=±5% resistance=220 package=THT]
  LED1 = LED - 5mm [color="Red (633nm)" package="5 mm [THT]"]
  U1 = Barometric Pressure Sensor

nets:
  N1: Arduino1.GND, LED1.cathode, U1.SCK
  N2: Arduino1.D7, U1.MISO
  N3: Arduino1.D6, U1.CSB
  +5V: Arduino1.+5V, U1.3.3V
  N4: R1.Pin_0, R2.Pin_0, R3.Pin_0, LED1.anode
  N5: R1.Pin_1, R2.Pin_1, R3.Pin_1
