# Fritzing sketch esquemaProjeto8 (saved by Fritzing 0.7.10b)
breadboards: 1

parts:
  R1 = Rotary Potentiometer (Small) [maximum_resistance=100kΩ]
  LED1 = LED - 5mm [color="Red (633nm)" package="5 mm [THT]"]
  LED2 = LED - 5mm [color="Red (633nm)" package="5 mm [THT]"]
  LED3 = LED - 5mm [color="Red (633nm)" package="5 mm [THT]"]
  Arduino1 = Arduino

nets:
  N1: R1.leg1, Arduino1.+5V
  N2: R1.wiper, Arduino1.A2
  N3: R1.leg2, LED1.anode, LED2.anode, LED3.anode, Arduino1.GND
  N4: LED1.cathode, Arduino1.D8
  N5: LED2.cathode, Arduino1.D13
  N6: LED3.cathode, Arduino1.D10
